# Fritzing sketch RTC schematics (saved by Fritzing 0.9.3b)
breadboards: 1

parts:
  LCD1 = LCD screen
  IC1 = DS1302 [package="DIP8 [THT]"]
  XTAL1 = CRYSTAL - kHz [frequency="32 kHz"]
  BAT1 = Battery Holders [package=battcom_20mm_pth]
  Часть1 = Arduino Uno (Rev3) - ICSP
  DHT1 = Humidity and Temperature Sensor DHT11
  R1 = Resistor [tolerance=±5% resistance=10k package="0603 [SMD]"]
  R2 = Trimmer Potentiometer [maximum_resistance=10kΩ package=THT]

nets:
  VSS: LCD1.VSS, LCD1.R/W, LCD1.LED-, Часть1.GND, DHT1.GND_2, R2.leg2
  VDD: LCD1.VDD, LCD1.LED+, IC1.+V, Часть1.5V, DHT1.Vcc, R1.Pin_1, R2.leg1
  N1: LCD1.V0, R2.wiper
  N2: LCD1.RS, Часть1.D7
  N3: LCD1.E, Часть1.D6_PWM
  N4: LCD1.DB4, Часть1.D5_PWM
  N5: LCD1.DB5, Часть1.D4
  N6: LCD1.DB6, Часть1.D3_PWM
  N7: LCD1.DB7, Часть1.D2
  N8: IC1.X1_-_Crystal, XTAL1.pin_0
  N9: IC1.X2_-_Crystal, XTAL1.pin_1
  N10: IC1.CE_-_Chip_Enable, Часть1.D10_PWM/SS
  N11: IC1.I/O_-_SPI_Data_In/Out, Часть1.D8
  N12: IC1.SCLK_-_SPI_Clock, Часть1.D9_PWM
  N13: IC1.Vbat_-_Backup_Supply, BAT1.+
  N14: Часть1.D11_PWM/MOSI, DHT1.Data-signal, R1.Pin_0

custom parts:
  Humidity and Temperature Sensor DHT11: Digital relative humidity & temperature sensor DHT11
